// Logisim project second half of the computer.circ as structural Verilog
module Right_shifter (
  input  shift_in,
  input  se_2,
  input  [7:0] \input ,
  input  se_1,
  output [7:0] \output ,
  output shift_out
);

  wire [6:0] register_1_q;

  Register register_1 (.D(\input ), .Q({shift_out, register_1_q}), .clk(se_1));  // open: en, clr
  Register register_2 (.D({register_1_q, shift_in}), .Q(\output ), .clk(se_2));  // open: en, clr

  // Notes on the sheet:
  //   It’s used for dividing numbers by 2 (e.g., 10101010, which is 170, becomes 01010101, which is 85) and for bit manipulation in programming.
  //   8-Bit Right Shifter
  //   An 8-bit right shifter is like a toy train with 8 cars (bits) on a track, sliding all the cars one spot to the right! If the input is 10101010, a right shift moves each bit one position right, turning 10101010 into 01010101—the rightmost bit (0) falls off, and a 0 is added on the left.
endmodule

module Left_shifter (
  input  se_2,
  input  [7:0] \input ,
  input  shift_in,
  input  se_1,
  output shift_out,
  output [7:0] \output 
);

  wire [7:1] register_1_q;

  Register register_1 (.D(\input ), .Q({register_1_q, shift_out}), .clk(se_1));  // open: en, clr
  Register register_2 (.D({shift_in, register_1_q}), .Q(\output ), .clk(se_2));  // open: en, clr

  // Notes on the sheet:
  //   8-Bit Left Shifter
  //   An 8-bit left shifter is like that same toy train, but sliding all 8 cars one spot to the left! So, 10101010 becomes 01010100—the leftmost bit (1) falls off, and a 0 is added on the right. It’s used for multiplying numbers by 2 (e.g., 10101010, which is 170, becomes 01010100, which is 84 in 8 bits due to overflow) and aligning bits in data processing.
endmodule

module Half_adder (
  input  a,
  input  b,
  output sum,
  output carry
);

  xor xor_1 (sum, a, b);
  and and_1 (carry, a, b);

  // Notes on the sheet:
  //   For example, if A = 1 and B = 1, C = 1; otherwise, C = 0.
  //   A half adder doesn’t handle a carry-in from a previous bit, so it’s only part of the story.
  //   For example, if A = 1 and B = 0, S = 1; if A = 1 and B = 1, S = 0.
  //   . Sum (S): The sum is 1 if exactly one car fits (A or B, but not both). This is an XOR operation: S = A XOR B.
  //   . Carry (C): The carry is 1 if both cars try to fit (A and B are both 1). This is an AND operation: C = A AND B.
  //   How it works
  //   A half adder is like a tiny toy calculator that adds two 1-bit numbers (A and B) and gives a 1-bit sum (S) and a 1-bit carry (C). Imagine two toy cars (A and B) trying to fit on one parking spot:
endmodule

module Full_adder (
  input  a,
  input  b,
  input  carry_in,
  output sum,
  output carry_out
);

  wire and_1_out, and_2_out, xor_1_out;

  xor xor_1 (xor_1_out, a, b);
  and and_1 (and_1_out, carry_in, xor_1_out);
  and and_2 (and_2_out, a, b);
  xor xor_2 (sum, xor_1_out, carry_in);
  or or_1 (carry_out, and_1_out, and_2_out);

  // Notes on the sheet:
  //   For example, if A = 1, B = 1, Cin = 0, Cout = 1 (from A AND B).
  //   For example, if A = 1, B = 1, Cin = 0, then S = 0 (1 + 1 + 0 = 10 in binary).
  //   . Sum (S): The sum is 1 if an odd number of inputs (A, B, Cin) are 1. This is an XOR of all three: S = A XOR B XOR Cin.
  //   . Carry-Out (Cout): The carry-out is 1 if at least two inputs are 1. This is: Cout = (A AND B) OR (A AND Cin) OR (B AND Cin).
  //   How it works
  //   A full adder is crucial because it’s like a super toy calculator that adds three bits at once—A, B, and a carry-in—making it possible to chain them together for adding big numbers like in our 8-bit adder, without missing any carryovers
  //   A full adder is like a bigger toy calculator that adds three 1-bit numbers: A, B, and a carry-in (Cin) from a previous addition, producing a 1-bit sum (S) and a 1-bit carry-out (Cout). It’s what we need for an 8-bit adder, where each bit position needs to handle a carry from the previous bit.
endmodule

module comparator (
  input  in_1,
  input  a__larger,
  input  a,
  input  b,
  output c,
  output all_bits_equal_so_far,
  output a__larger_2
);

  wire _2_out, _4_out;

  xor _1 (c, a, b);
  not _2 (_2_out, c);
  and _3 (all_bits_equal_so_far, _2_out, in_1);
  and _4 (_4_out, in_1, a, c);
  or _5 (a__larger_2, _4_out, a__larger);

  // Notes on the sheet:
  //   Function:
  //   Inputs:
  //   Outputs:
  //   . Bits a and b (the bits being compared).
  //   A single bit comparator is a circuit that compares two bits, a and b
  //   . “All bits above are equal” (1 if higher bits match; a constant 1 for the top unit).
  //   . “Equal”: From a NOT-XOR gate, outputs 1 if a = b, showing the bits match.
  //   unequal
  //   equal
  //   . “A larger from above” (1 if ‘a’ is already determined to be larger; a constant 0 for the top unit).
  //   . ‘c’: From an XOR gate (a XOR b), outputs 1 if a ≠ b, indicating a difference at this position.
  //   The outputs are passed to the next unit to continue the comparison, helping comparing 16 bits.
  //   all bits above are equal
  //   How it works
  //   . “A larger”: Outputs 1 if a = 1, b = 0 (a is larger, and 0 if a is smaller than b), and all higher bits are equal (computed by ANDing a[i], the XOR output, and the “all bits above are equal” input).
endmodule

module _8_bit_comparator (
  input  in_1,
  input  _128,
  input  _64,
  input  _32,
  input  _16,
  input  _8,
  input  _4,
  input  _2,
  input  _1,
  input  _128_2,
  input  _64_2,
  input  _32_2,
  input  _16_2,
  input  _8_2,
  input  _4_2,
  input  _2_2,
  input  _1_2,
  output out_18,
  output out_19,
  output out_20,
  output c,
  output out_22,
  output out_23,
  output out_24,
  output out_25,
  output equal,
  output a__larger
);

  wire comparator_1_a__larger_2, comparator_1_all_bits_equal_so_far, comparator_2_a__larger_2,
       comparator_2_all_bits_equal_so_far, comparator_3_a__larger_2, comparator_3_all_bits_equal_so_far,
       comparator_4_a__larger_2, comparator_4_all_bits_equal_so_far, comparator_5_a__larger_2,
       comparator_5_all_bits_equal_so_far, comparator_6_a__larger_2, comparator_6_all_bits_equal_so_far,
       comparator_7_a__larger_2, comparator_7_all_bits_equal_so_far;

  comparator comparator_1 (
    .a(_128), .b(_128_2), .in_1(1'b1), .a__larger(in_1),
    .all_bits_equal_so_far(comparator_1_all_bits_equal_so_far), .a__larger_2(comparator_1_a__larger_2),
    .c(out_18));
  comparator comparator_2 (
    .a(_64), .b(_64_2), .in_1(comparator_1_all_bits_equal_so_far), .a__larger(comparator_1_a__larger_2),
    .all_bits_equal_so_far(comparator_2_all_bits_equal_so_far), .a__larger_2(comparator_2_a__larger_2),
    .c(out_19));
  comparator comparator_3 (
    .a(_32), .b(_32_2), .in_1(comparator_2_all_bits_equal_so_far), .a__larger(comparator_2_a__larger_2),
    .all_bits_equal_so_far(comparator_3_all_bits_equal_so_far), .a__larger_2(comparator_3_a__larger_2),
    .c(out_20));
  comparator comparator_4 (
    .a(_16), .b(_16_2), .in_1(comparator_3_all_bits_equal_so_far), .a__larger(comparator_3_a__larger_2),
    .all_bits_equal_so_far(comparator_4_all_bits_equal_so_far), .a__larger_2(comparator_4_a__larger_2), .c(c));
  comparator comparator_5 (
    .a(_8), .b(_8_2), .in_1(comparator_4_all_bits_equal_so_far), .a__larger(comparator_4_a__larger_2),
    .all_bits_equal_so_far(comparator_5_all_bits_equal_so_far), .a__larger_2(comparator_5_a__larger_2),
    .c(out_22));
  comparator comparator_6 (
    .a(_4), .b(_4_2), .in_1(comparator_5_all_bits_equal_so_far), .a__larger(comparator_5_a__larger_2),
    .all_bits_equal_so_far(comparator_6_all_bits_equal_so_far), .a__larger_2(comparator_6_a__larger_2),
    .c(out_23));
  comparator comparator_7 (
    .a(_2), .b(_2_2), .in_1(comparator_6_all_bits_equal_so_far), .a__larger(comparator_6_a__larger_2),
    .all_bits_equal_so_far(comparator_7_all_bits_equal_so_far), .a__larger_2(comparator_7_a__larger_2),
    .c(out_24));
  comparator comparator_8 (
    .a(_1), .b(_1_2), .in_1(comparator_7_all_bits_equal_so_far), .a__larger(comparator_7_a__larger_2),
    .all_bits_equal_so_far(equal), .a__larger_2(a__larger), .c(out_25));
  comparator comparator_9 ();  // open: a, b, in_1, a__larger, all_bits_equal_so_far, a__larger_2, c

  // Notes on the sheet:
  //   Inputs:
  //   Outputs:
  //   Function:
  //   Example:
  //   . ‘a’ = 128+64+1 (11000001, 193), ‘b’ = 10101010 (170).
  //   . Bits a[i] and b[i] (e.g., a[7] and b[7] for the top unit).
  //   . Contributes to the final “equal” and “a larger” outputs.
  //   a
  //   b
  //   . c’: From an XOR gate (a[i] XOR b[i]), outputs 1 if bits differ, used for zero detection or difference checking.
  //   . “Equal”: Outputs 1 if all bits match (computed by ANDing all “equal” outputs from each unit), meaning ‘a’ = ‘b’.
  //   . At bit 6: a[6] = 1, b[6] = 0, bit 7 matches, so “a larger” is 1, “equal” is 0, and ‘c’ at bit 6 is 1 (bits differ).
  //   How it works
  //   . “All bits above are equal” and “a larger from above” signals from the previous unit (or constants for the top unit).
  //   . “A larger”: Outputs 1 if ‘a’ > ‘b’ (determined by the first unit where a[i] = 1, b[i] = 0, and higher bits are equal, propagated through OR gates).
  //   Approach: The Comparator as an Enigma Codebreaker
  //   An 8-bit comparator compares two 8-bit inputs, ‘a[i]’ and ‘b[i]’ (16 bits total), using 8 single bit comparators stacked from bit 7 (most significant) to bit 0 (least significant), functioning like a complete Enigma machine deciphering two 8-bit messages.
  //   Imagine the 8-bit comparator as a World War II Enigma machine, used by codebreakers like Alan Turing to decipher enemy messages. Each single bit comparator is like a rotor in the Enigma, analyzing one pair of letters (bits a[i] and b[i]) in a coded message.
  //   The static 1 and 0 at the top are the initial settings of the machine, starting the decoding process. The full 8-bit comparator, with its 8 rotors, deciphers the entire message (‘a’ vs. ‘b’), outputting whether the codes are identical (“equal”) or if one is greater (“a larger”), just like breaking an 8-letter Enigma code to reveal a hidden instruction.
  //   The rotor’s job is to check if the letters match (‘c’ output: 1 if they differ, like spotting a mismatch in the code), if they’re the same (“equal” output: 1 if a[i] = b[i], like confirming a correct letter pair), and if one letter is “larger” (a[i] = 1, b[i] = 0, like determining which code has a higher value at this position). The “all bits above are equal” signal is like a codebreaker’s log, ensuring all previous letters matched before deciding which code is “larger.”
endmodule

module ALU (
  input  [7:0] a,
  input  [7:0] b,
  input  carry_in,
  input  should_be_always_0,
  input  [2:0] op_code,
  output zero,
  output [7:0] out_7,
  output carry_out,
  output a__larger,
  output equal
);

  wire and_2_out, and_3_out, decoder_1_out0, decoder_1_out1, decoder_1_out2, decoder_1_out3, decoder_1_out4,
       decoder_1_out5, decoder_1_out6, Lclk_out, or_2_out, Rclk_out, SHL_shift_out, SHR_shift_out;
  wire [7:0] ADD_out_18, and_1_out, not_1_out, or_1_out, SHL_output, SHR_output, xor_1_out;

  assign xor_1_out = a ^ b;  // XOR_Gate xor_1, 8 bits wide
  assign or_1_out = a | b;  // OR_Gate or_1, 8 bits wide
  assign and_1_out = a & b;  // AND_Gate and_1, 8 bits wide
  assign not_1_out = ~b;  // NOT_Gate not_1, 8 bits wide
  Left_shifter SHL (
    .\input (a), .shift_in(carry_in), .se_1(and_2_out), .se_2(and_2_out), .shift_out(SHL_shift_out),
    .\output (SHL_output));
  and and_2 (and_2_out, Lclk_out, decoder_1_out4);
  Right_shifter SHR (
    .shift_in(carry_in), .\input (a), .se_1(and_3_out), .se_2(and_3_out), .\output (SHR_output),
    .shift_out(SHR_shift_out));
  Clock Rclk (.out(Rclk_out));
  and and_3 (and_3_out, Rclk_out, decoder_1_out5);
  _8_bit_comparator ADD (
    ._128(a[7]), ._64(a[6]), ._32(a[5]), ._16(a[4]), ._8(a[3]), ._4(a[2]), ._2(a[1]), ._1(a[0]),
    ._128_2(b[7]), ._64_2(b[6]), ._32_2(b[5]), ._16_2(b[4]), ._8_2(b[3]), ._4_2(b[2]), ._2_2(b[1]),
    ._1_2(b[0]), .in_1(should_be_always_0), .equal(equal), .a__larger(a__larger), .out_18(ADD_out_18[0]),
    .out_19(ADD_out_18[1]), .out_20(ADD_out_18[2]), .c(ADD_out_18[3]), .out_22(ADD_out_18[4]),
    .out_23(ADD_out_18[5]), .out_24(ADD_out_18[6]), .out_25(ADD_out_18[7]));
  Clock Lclk (.out(Lclk_out));
  Decoder #(.select(3)) decoder_1 (
    .out0(decoder_1_out0), .out1(decoder_1_out1), .out2(decoder_1_out2), .out3(decoder_1_out3),
    .out4(decoder_1_out4), .out5(decoder_1_out5), .out6(decoder_1_out6), .sel(op_code));  // open: out7, en
  assign out_7 = decoder_1_out0 ? xor_1_out : 8'bz;  // Controlled_Buffer controlled_buffer_1
  assign out_7 = decoder_1_out1 ? or_1_out : 8'bz;  // Controlled_Buffer controlled_buffer_2
  assign out_7 = decoder_1_out2 ? and_1_out : 8'bz;  // Controlled_Buffer controlled_buffer_3
  assign out_7 = decoder_1_out3 ? not_1_out : 8'bz;  // Controlled_Buffer controlled_buffer_4
  assign out_7 = decoder_1_out4 ? SHL_output : 8'bz;  // Controlled_Buffer controlled_buffer_5
  assign out_7 = decoder_1_out5 ? SHR_output : 8'bz;  // Controlled_Buffer controlled_buffer_6
  assign out_7 = decoder_1_out6 ? ADD_out_18 : 8'bz;  // Controlled_Buffer controlled_buffer_7
  or or_2 (or_2_out, out_7[0], out_7[1], out_7[2], out_7[3], out_7[4], out_7[5], out_7[6], out_7[7]);
  not not_2 (zero, or_2_out);
  or or_3 (carry_out, SHL_shift_out, SHR_shift_out);

  // Notes on the sheet:
  //   7 Tools:
  //   . AND: Checks where ‘a’ and ‘b’ both have 1s.
  //   . NOT: Flips ‘a’ (turns 1s to 0s and 0s to 1s).
  //   How It Works
  //   Why It’s Cool
  //   It has 7 tools inside, and you pick one tool at a time to use!
  //   . XOR: Mixes ‘a’ and ‘b’ in a special way (like a secret code).
  //   . OR: Combines ‘a’ and ‘b’ (if either has a 1, the result gets a 1).
  //   . SHL: Slides ‘a’ left by 1 spot (like 10101010 becomes 01010100).
  //   . SHR: Slides ‘a’ right by 1 spot (like 10101010 becomes 01010101).
  //   . Comparator: Tells if ‘a’ is bigger than ‘b’ or if they’re the same.
  //   . A decoder (like a tool selector) turns on one tool using the “op” code.
  //   . The tool’s 8-bit result goes to the “Result” output, but only one tool works at a time!
  //   . You give it ‘a’, ‘b’, a “Carry In” bit, and a 3-bit “op” code to pick the tool (like 000 for XOR, 100 for SHL).
  //   Approach :The ALU is a Toolbox!
  //   What’s Inside the Toolbox?
  //   . Extra outputs: “Zero” (lights up if Result is 00000000), “A Larger” (lights up if ‘a’ is bigger), and “Equal” (lights up if ‘a’ equals ‘b’).
  //   Think of the ALU as a magical toolbox that helps your computer do math and logic stuff with two 8-bit numbers, ‘a’ and ‘b’ (like 10101010 and 11001100).
  //   The ALU is your computer’s handyman, doing all the math and comparing jobs, and the clock makes sure SHL and SHR work at the right time!
  //   . SHL and SHR have little storage boxes (registers) that save their inputs and outputs, and they only work when a clock (clk) says “go” (clk = 1). We’ll explain the clock next chapter—it’s like a timer that keeps everything in sync!
endmodule

module bus_1 (
  input  MSB,
  input  in_2,
  input  in_3,
  input  in_4,
  input  in_5,
  input  in_6,
  input  in_7,
  input  LSB,
  input  bus_1,
  input  [7:0] OUTPUT
);

  wire not_1_out;

  and and_1 (OUTPUT[7], MSB, not_1_out);
  and and_2 (OUTPUT[6], in_2, not_1_out);
  and and_3 (OUTPUT[5], in_3, not_1_out);
  and and_4 (OUTPUT[4], in_4, not_1_out);
  and and_5 (OUTPUT[3], in_5, not_1_out);
  and and_6 (OUTPUT[2], in_6, not_1_out);
  and and_7 (OUTPUT[1], in_7, not_1_out);
  not not_1 (not_1_out, bus_1);
  or or_1 (OUTPUT[0], LSB, bus_1);
endmodule

// clk d
module clock (
  input  clk,
  input  clk_2,
  input  clk_3,
  input  clk_4,
  input  clk_5,
  output clk_e,
  output clk_s,
  output out_8
);

  not not_1 (clk_2, clk_2);
  not not_2 (clk_4, clk_4);
  not not_3 (clk, clk);
  Clock clock_1 (.out(out_8));
  or or_1 (clk_e, clk_4, clk_4);
  and and_1 (clk_s, clk_4, clk_4);

  assign clk_3 = clk_2;
  assign clk_5 = clk_4;

  // Notes on the sheet:
  //   How it works
  //   To slow it down, you add a longer wire or use a resistor (delaying the signal by about a quarter of a cycle):
  //   It’s made by connecting a NOT gate’s output back to its input, creating a loop that keeps flipping the bit (1 → 0 → 1 → 0 …):
  //   . The clock sets the pace for the whole computer, like a drummer keeping the beat.
  //   . Add the Clock: Go to the “Wiring” library in Logisim, pick the “Clock” component, and place it in your circuit.
  //   Now we're going to do something fairly simple. We will take the original clock and the delayed clock, and both AND them and OR them to create two new bits, like so:
  //   . Set the Ticks: Double-click the Clock to set its timing. “High Duration” is how long it’s on (1), and “Low Duration” is how long it’s off (0). For example, set both to 1 tick for a simple 0, 1, 0, 1 pattern.
  //   . Make It Work: To see the clock in action, press Ctrl+K (or go to Simulate → Ticks Enabled). This starts the ticks, and the clock will flip between 0 and 1 automatically during the simulation.
  //   . The clock’s job is to time when data moves: first, enable a “from” register to send data on the bus, then enable a “to” register to capture it, ensuring the “to” register grabs the data before the “from” register turns off.
  //   . clk e (from the OR): This signal turns on first and stays on longer. It’s like opening a gate to let the first storage box put its number onto the bus, giving the number plenty of time to travel.
  //   These three circuits are just to explain how a clock works—we don’t need to build them in Logisim. Logisim has a built-in Clock component that already gives us a clock signal (0, 1, 0, 1 …), so we’ll use that instead to save time and keep things simple.
  //   . Why This Timing Matters: Since clk e stays on longer, the number is ready on the bus when clk s turns on. This makes sure the second storage box gets the correct number before the first storage box stops sending it, avoiding any mistakes.
  //   The clock is a bit that flips between on (1) and off (0) super fast :billions of times per second, or gigahertz ( it was decided to use a name of a nerd scientist who lived in Germany who did some of the early research in 1800's that led up to radio to use his name to describe how fast electricity was going on and off persecond )setting the timing for the whole computer.
  //   . clk s (from the AND): This signal turns on later, right in the middle of when clk e is on, and it’s on for a shorter time. It’s like opening a second gate to let another storage box grab the number from the bus and save it, but only after the number has had time to arrive safely.
  //   The third circuit is really helpful because it makes two special signals—clk e and clk s—that work together to move data safely inside the computer. Imagine the computer has little storage boxes (we’ll call them storage boxes for now) that hold numbers, like 10101010. We need to move a number from one storage box to another through a shared path called the bus, but we have to make sure the number doesn’t get mixed up or lost.
endmodule

module clock_we_gonna_use (
  output clk_e,
  output clk_s
);

  wire clk_d_out, clk_out;

  Clock clk (.out(clk_out));
  Clock #(.highDuration(2)) clk_d (.out(clk_d_out));
  or or_1 (clk_e, clk_out, clk_d_out);
  and and_1 (clk_s, clk_out, clk_d_out);

  // Notes on the sheet:
  //   1 tick on high/low
  //   2 ticks on high
  //   Ticks and Clock Speed:
  //   . The Clock component has two settings: “High Duration” (how many ticks the clock is on, or 1) and “Low Duration” (how many ticks it’s off, or 0).
  //   . It’s In Logisim, a “tick” is like a tiny step in the simulation—it’s how time moves forward. by connecting a NOT gate’s output back to its input, creating a loop that keeps flipping the bit (1 → 0 → 1 → 0 …):
  //   . If you make the High Duration longer (more ticks), the clock stays on longer, which slows down the overall on-off cycle. For example, High Duration of 2 ticks and Low Duration of 1 tick means the clock is on for 2 ticks, off for 1 tick, repeating every 3 ticks—slower than 1 tick on, 1 tick off.
endmodule
